# Fritzing sketch Diagrama (saved by Fritzing 0.9.9b)
breadboards: 1

parts:
  LED1 = smd LED [color="Red (633nm)" package="0603 [SMD]"]
  Componente1 = Thumb Joystick
  Part3 = RFID-RC522-v2
  S2 = Pushbutton [package="[SMD]"]
  Componente2 = Arduino Uno (Rev3) - ICSP
  Mod1 = Passive Buzzer
  R1 = Resistor [tolerance=±5% resistance=10000 power=0.23W package="0402 [SMD]"]
  R2 = Resistor [tolerance=±5% resistance=330 package="0402 [SMD]"]

nets:
  GND: LED1.cathode, Componente1.GND, Part3.GND, Componente2.GND, Mod1.-, R1.Pin_1
  N1: LED1.anode, R2.Pin_0
  N2: Componente1.SEL, Componente2.D5_PWM
  N3: Componente1.HORZ, Componente2.A5/SCL
  N4: Componente1.VERT, Componente2.A4/SDA
  VCC: Componente1.VCC, S2.Pin_3, S2.Pin_4, Componente2.5V, Mod1.S
  N5: Part3.SDA, Componente2.D10_PWM/SS
  N6: Part3.SCK, Componente2.D13/SCK
  N7: Part3.MOSI, Componente2.ICSP_MOSI, Componente2.D11_PWM/MOSI
  N8: Part3.MISO, Componente2.D12/MISO
  N9: Part3.RST, Componente2.D9_PWM
  N10: Part3.3_3V, Componente2.3V3
  N11: S2.Pin_1, S2.Pin_2, Componente2.D2, R1.Pin_0
  N12: Componente2.D8, Mod1.NC
  N13: Componente2.D6_PWM, R2.Pin_1

custom parts:
  RFID-RC522-v2: A simple China made RFID-RC522 Reader; do check the pin labels, as this is a MFRC522 based clone.
